# Fritzing sketch roomba_wall (saved by Fritzing 0.9.2b)
breadboards: 1

parts:
  TRINKET2 = Trinket 5V
  R4 = Resistor [tolerance=±5% resistance=22 package=THT]
  Q2 = NPN-Transistor [package="TO92 [THT]"]
  R5 = Resistor [tolerance=±5% resistance=47 package=THT]
  LED3 = LED - 5mm [color="Infrared (940nm)" package="5 mm [THT]"]
  R6 = Resistor [tolerance=±5% resistance=220 package=THT]
  LED4 = LED - 5mm [color="Red (633nm)" package="5 mm [THT]"]

nets:
  N1: TRINKET2.no_name_yet#2, Q2.C, LED4.cathode
  N2: TRINKET2.no_name_yet#3, R6.Pin_0
  N3: TRINKET2.no_name_yet#6, R5.Pin_0
  N4: TRINKET2.no_name_yet#8, R4.Pin_0
  N5: R4.Pin_1, Q2.B
  N6: Q2.E, LED3.cathode
  N7: R5.Pin_1, LED3.anode
  N8: R6.Pin_1, LED4.anode

custom parts:
  Trinket 5V: Adafruit Trinket 5V
